# Fritzing sketch basicSetup (saved by Fritzing 0.9.3b)
breadboards: 1

parts:
  Teensy1 = Teensy 3.6 (Basic)
  Raspberry_Pi_1 = Raspberry Pi 3 [part_number=RPI-3-V1.2]

nets:
  GND: Teensy1.GND, Teensy1.GND1, Raspberry_Pi_1.GND
  N1: Teensy1.D0, Raspberry_Pi_1.GIPO14
  N2: Teensy1.D1, Raspberry_Pi_1.GIPO15
  N3: Teensy1.3V3, Teensy1.3V3_1

custom parts:
  Teensy 3.6 (Basic): The Teensy is a complete USB-based microcontoller development system, in a very small footprint, capable of implementing many types of projects. All programming is done via the USB port. No special programmer is needed, only a standard micro-USB cable and a PC or Macintosh with a USB port.
